# Fritzing sketch playsdcard (saved by Fritzing 0.9.3b)
breadboards: 1

parts:
  Part1 = Arduino Uno (Rev3)
  LM386 = LM386 [package=dip08]
  R1 = Resistor [tolerance=±5% resistance=1k package=THT]
  R2 = Resistor [tolerance=±5% resistance=10k package=THT]
  10µF = Electrolytic Capacitor [capacitance=1µF package="100 mil [THT, electrolytic]"]
  SP1 = SPEAKER [package=pcb_mount_speaker]
  100µF = Electrolytic Capacitor [capacitance=10µF voltage=20V package="100 mil [THT, electrolytic]"]
  10µF_2 = Electrolytic Capacitor [capacitance=10µF voltage=20V package="100 mil [THT, electrolytic]"]
  Part2 = MicroSD Card Module
  100µF_2 = Electrolytic Capacitor [capacitance=1µF package="100 mil [THT, electrolytic]"]

nets:
  N1: Part1.D9_PWM, R1.Pin_1
  N2: Part1.D10_PWM/SS, Part2.CS
  N3: Part1.D11_PWM/MOSI, Part2.MOSI
  N4: Part1.D12/MISO, Part2.MISO
  N5: Part1.D13/SCK, Part2.SCK
  GND: Part1.GND, LM386.-IN, LM386.V-, Part2.GND, 100µF_2.-
  5V: Part1.5V, LM386.V+, Part2.VCC, 100µF_2.+
  N6: LM386.GAIN, 10µF_2.-, 10µF_2.+
  N7: LM386.+IN, R1.Pin_0
  N8: LM386.OUT, R2.Pin_0, 100µF.+
  N9: R2.Pin_1, 10µF.+
  N10: 10µF.-, SP1.-
  N11: SP1.+, 100µF.-
